# Fritzing sketch CTRL_Motor (saved by Fritzing 0.9.3b)
circuit board: 10.9cm x 10.9cm
breadboards: 1

parts:
  R13 = Resistor [tolerance=±5% resistance=220 package=THT]
  J18 = shrouded pin header, 16 pins [form="♂ (shrouded male)"]
  R14 = Resistor [tolerance=±5% resistance=220 package=THT]
  J19 = shrouded pin header, 16 pins [form="♂ (shrouded male)"]
  J20 = female pin header, 4 pins [form="♀ (female)"]
  J21 = female pin header, 10 pins [form="♀ (female)"]
  HLK-PM4 = HLK-PM01
  R15 = Resistor [tolerance=±5% resistance=10k package=THT]
  R16 = Resistor [tolerance=±5% resistance=10k package=THT]
  Part4 = Arduino Nano (Rev3.0)
  J22 = female pin header, 2 pins [form="♀ (female)"]
  J23 = female pin header, 7 pins [form="♀ (female)"]
  J26 = rounded female pin header, 7 pins [form="♀ (female rounded)"]
  J27 = female pin header, 7 pins [form="♀ (female)"]
  U7 = 7400 [package=dil14]
  U8 = 7400 [package=dil14]

nets:
  N1: R13.Pin_0, Part4.D9
  N2: R13.Pin_1, J18.pin12
  N3: J18.pin1, R15.Pin_0
  N4: J18.pin2, R16.Pin_0
  N5: J18.pin3, J18.pin4, J18.pin5, J18.pin8, HLK-PM4.-Vo, R15.Pin_1, R16.Pin_1, Part4.GND, J23.pin1, J23.pin7
  N6: J18.pin9, HLK-PM4.+Vo, Part4.VIN, J23.pin4, J23.pin5
  N7: J18.pin10, Part4.A4
  N8: J18.pin11, Part4.A5
  N9: J18.pin13, R14.Pin_1
  N10: J18.pin14, Part4.RESET
  N11: J18.pin15, Part4.D2
  N12: J18.pin16, Part4.D3
  N13: R14.Pin_0, Part4.D8
  N14: J19.pin1, J21.pin2
  N15: J19.pin2, J21.pin4
  N16: J19.pin3, J21.pin6
  N17: J19.pin4, J21.pin8
  N18: J19.pin5, J21.pin10
  N19: J19.pin8, J20.pin4
  N20: J19.pin9, J20.pin3
  N21: J19.pin10, J20.pin2
  N22: J19.pin11, J20.pin1
  N23: J19.pin12, J21.pin9
  N24: J19.pin13, J21.pin7
  N25: J19.pin14, J21.pin5
  N26: J19.pin15, J21.pin3
  N27: J19.pin16, J21.pin1
  N28: HLK-PM4.AC#0, J22.pin2
  N29: HLK-PM4.AC#1, J22.pin1
  N30: Part4.D10, J23.pin6
  N31: Part4.D11/MOSI, J23.pin3
  N32: Part4.D12/MISO, J23.pin2
  N33: J26.pin1, J27.pin7
  N34: J26.pin2, J27.pin6
  GND: J26.pin3, J26.pin4, J27.pin4, J27.pin5, U7.GND, U8.GND
  N35: J26.pin5, U7.A1I, U7.A2I, U8.B2I
  N36: J26.pin6, U7.B2I, U8.A1I, U8.A2I
  VCC: J26.pin7, J27.pin1, U7.VCC, U8.VCC
  N37: J27.pin2, U8.DO
  N38: J27.pin3, U7.DO
  N39: U7.AO, U7.B1I
  N40: U7.BO, U7.D1I, U7.D2I
  N41: U8.AO, U8.B1I
  N42: U8.BO, U8.D1I, U8.D2I

custom parts:
  7400: Quad NAND gate
